# Fritzing sketch EE (saved by Fritzing 0.9.3b)
breadboards: 1

parts:
  R1 = Resistor [tolerance=±5% resistance=10k package=THT]
  R3 = Resistor [tolerance=±5% resistance=10k package=THT]
  R4 = Resistor [tolerance=±5% resistance=10k package=THT]
  R5 = Resistor [tolerance=±5% resistance=10k package=THT]
  R6 = Resistor [tolerance=±5% resistance=10k package=THT]
  FR1 = Basic Flex Resistor
  FR2 = Basic Flex Resistor
  FR3 = Basic Flex Resistor
  FR4 = Basic Flex Resistor
  FR5 = Basic Flex Resistor
  Arduino_Mega = Arduino Mega 2560 (Rev3)

nets:
  N1: R1.Pin_0, FR1.pin_1, Arduino_Mega.A4
  N2: R1.Pin_1, R3.Pin_1, R4.Pin_1, R5.Pin_1, R6.Pin_1, Arduino_Mega.5V
  N3: R3.Pin_0, FR2.pin_1, Arduino_Mega.A3
  N4: R4.Pin_0, FR3.pin_1, Arduino_Mega.A2
  N5: R5.Pin_0, FR4.pin_1, Arduino_Mega.A1
  N6: R6.Pin_0, FR5.pin_1, Arduino_Mega.A0
  N7: FR1.Pin_2, FR2.Pin_2, FR3.Pin_2, FR4.Pin_2, FR5.Pin_2, Arduino_Mega.GND
